# Fritzing sketch IRtoRokuBridge (saved by Fritzing 0.9.3b)
breadboards: 1

parts:
  U1 = NodeMCU V1.0
  IR1 = TSOP312.., 314.. [package=THT]

nets:
  N1: U1.3V3, IR1.Vs
  GND: U1.GND, IR1.GND
  N2: U1.D5, IR1.Data

custom parts:
  NodeMCU V1.0: ESP9266 based NodeMCU
